# Fritzing sketch Press_Machine_Bread_Board (saved by Fritzing 0.9.3b)
breadboards: 1

parts:
  Part1 = Arduino Uno (Rev3) - ICSP
  R2 = Resistor [tolerance=±5% resistance=220 package="0805 [SMD]"]
  LED1 = smd LED [color="Red (633nm)" package="0805 [SMD]"]
  LED2 = smd LED [color="Green (560nm)" package="0805 [SMD]"]
  LED3 = smd LED [color="Blue (470nm)" package="0805 [SMD]"]
  R3 = Resistor [tolerance=±5% resistance=220 package="0805 [SMD]"]
  R4 = Resistor [tolerance=±5% resistance=220 package="0805 [SMD]"]
  J1 = Basic Servo

nets:
  N1: Part1.D8, R2.Pin_1
  N2: Part1.D9_PWM, J1.pulse
  N3: Part1.D12/MISO, Part1.D13/SCK, R4.Pin_1
  N4: Part1.D7, R3.Pin_1
  5V: Part1.5V, J1.vcc
  GND: Part1.GND, LED1.cathode, LED2.cathode, LED3.cathode, J1.gnd
  N5: R2.Pin_0, LED1.anode
  N6: LED2.anode, R3.Pin_0
  N7: LED3.anode, R4.Pin_0
